# Fritzing sketch schematic (saved by Fritzing 0.9.0b)
breadboards: 1

parts:
  LCD1 = LCD screen
  Raspberry_Pi1 = Raspberry Pi B+
  play_pause = Pushbutton [package="[THT]"]
  skip = Pushbutton [package="[THT]"]
  volume_up = Pushbutton [package="[THT]"]
  volume_down = Pushbutton [package="[THT]"]
  R1 = Trimmer Potentiometer [maximum_resistance=10kΩ package=THT]

nets:
  VSS: LCD1.VSS, LCD1.R/W, LCD1.LED-, Raspberry_Pi1.GND, play_pause.Pin_1, play_pause.Pin_2, skip.Pin_3, skip.Pin_4, volume_up.Pin_1, volume_up.Pin_2, volume_down.Pin_3, volume_down.Pin_4, R1.leg1
  VDD: LCD1.VDD, Raspberry_Pi1.5V, R1.leg2
  N1: LCD1.V0, R1.wiper
  N2: LCD1.RS, Raspberry_Pi1.GIPO12
  N3: LCD1.E, Raspberry_Pi1.GIPO21
  N4: LCD1.DB4, Raspberry_Pi1.GIPO5
  N5: LCD1.DB5, Raspberry_Pi1.GIPO6
  N6: LCD1.DB6, Raspberry_Pi1.GIPO13
  N7: LCD1.DB7, Raspberry_Pi1.GIPO26
  N8: LCD1.LED+, Raspberry_Pi1.GIPO25
  N9: Raspberry_Pi1.GIPO20, volume_up.Pin_3, volume_up.Pin_4
  N10: Raspberry_Pi1.GIPO16, volume_down.Pin_1, volume_down.Pin_2
  N11: Raspberry_Pi1.GIPO23, skip.Pin_1, skip.Pin_2
  N12: Raspberry_Pi1.GIPO18, play_pause.Pin_3, play_pause.Pin_4
